// Logisim project 2106047_AYUSH_LAB1(1).circ as structural Verilog: 1 circuit, main circuit main
module main (
  input  A0,
  input  A1,
  input  A16,
  input  B0,
  input  A17,
  input  B1,
  input  B16,
  input  B17,
  input  Cin,
  input  A2,
  input  A3,
  input  A18,
  input  B2,
  input  A19,
  input  B3,
  input  B18,
  input  B19,
  input  A4,
  input  A5,
  input  A20,
  input  B4,
  input  A21,
  input  B5,
  input  B20,
  input  B21,
  input  A6,
  input  A7,
  input  A22,
  input  B6,
  input  A23,
  input  B7,
  input  B22,
  input  B23,
  input  A8,
  input  A9,
  input  A24,
  input  B8,
  input  A25,
  input  B9,
  input  B24,
  input  B25,
  input  A10,
  input  A11,
  input  A26,
  input  B10,
  input  A27,
  input  B11,
  input  B26,
  input  B27,
  input  A12,
  input  A13,
  input  A28,
  input  B12,
  input  A29,
  input  B13,
  input  B28,
  input  B29,
  input  A14,
  input  A15,
  input  A30,
  input  B14,
  input  A31,
  input  B15,
  input  B30,
  input  B31,
  output S0,
  output S1,
  output S16,
  output S17,
  output S2,
  output S3,
  output S18,
  output S19,
  output S4,
  output S5,
  output S20,
  output S21,
  output S6,
  output S7,
  output S22,
  output S23,
  output S8,
  output S9,
  output S24,
  output S25,
  output S10,
  output S11,
  output S26,
  output S27,
  output S12,
  output S13,
  output S28,
  output S29,
  output S14,
  output S15,
  output S30,
  output S31,
  output Cout
);

  wire and_1_out, and_2_out, and_3_out, and_4_out, and_5_out, and_6_out, and_7_out, and_8_out, and_9_out,
       and_10_out, and_11_out, and_12_out, and_13_out, and_14_out, and_15_out, and_16_out, and_17_out,
       and_18_out, and_19_out, and_20_out, and_21_out, and_22_out, and_23_out, and_24_out, and_25_out,
       and_26_out, and_27_out, and_28_out, and_29_out, and_30_out, and_31_out, and_32_out, and_33_out,
       and_34_out, and_35_out, and_36_out, and_37_out, and_38_out, and_39_out, and_40_out, and_41_out,
       and_42_out, and_43_out, and_44_out, and_45_out, and_46_out, and_47_out, and_48_out, and_49_out,
       and_50_out, and_51_out, and_52_out, and_53_out, and_54_out, and_55_out, and_56_out, and_57_out,
       and_58_out, and_59_out, and_60_out, and_61_out, and_62_out, and_63_out, and_64_out, or_1_out,
       or_2_out, or_3_out, or_4_out, or_5_out, or_6_out, or_7_out, or_8_out, or_11_out, or_12_out, or_13_out,
       or_16_out, or_17_out, or_18_out, or_19_out, or_20_out, or_21_out, or_22_out, or_23_out, or_25_out,
       or_27_out, or_28_out, or_29_out, xor_1_out, xor_2_out, xor_3_out, xor_7_out, xor_8_out, xor_10_out,
       xor_11_out, xor_12_out, xor_13_out, xor_17_out, xor_19_out, xor_21_out, xor_24_out, xor_25_out,
       xor_28_out, xor_30_out, xor_33_out, xor_34_out, xor_36_out, xor_38_out, xor_40_out, xor_41_out,
       xor_42_out, xor_45_out, xor_46_out, xor_48_out, xor_50_out, xor_54_out, xor_55_out, xor_58_out,
       xor_60_out, xor_63_out;

  xor xor_1 (xor_1_out, A0, B0);
  and and_1 (and_1_out, xor_1_out, Cin);
  and and_2 (and_2_out, A0, B0);
  xor xor_2 (xor_2_out, A2, B2);
  and and_3 (and_3_out, A2, B2);
  xor xor_3 (xor_3_out, A4, B4);
  xor xor_4 (S0, xor_1_out, Cin);
  xor xor_5 (S2, xor_2_out, or_7_out);
  and and_4 (and_4_out, xor_2_out, or_7_out);
  and and_5 (and_5_out, xor_3_out, A4);
  and and_6 (and_6_out, A4, B4);
  or or_1 (or_1_out, and_1_out, and_2_out);
  or or_2 (or_2_out, and_4_out, and_3_out);
  xor xor_6 (S4, xor_3_out, A4);
  xor xor_7 (xor_7_out, A6, B6);
  and and_7 (and_7_out, A6, B6);
  xor xor_8 (xor_8_out, A8, B8);
  or or_3 (or_3_out, and_5_out, and_6_out);
  xor xor_9 (S6, xor_7_out, A6);
  and and_8 (and_8_out, xor_7_out, A6);
  and and_9 (and_9_out, xor_8_out, or_12_out);
  and and_10 (and_10_out, A8, B8);
  xor xor_10 (xor_10_out, A10, B10);
  and and_11 (and_11_out, A10, B10);
  xor xor_11 (xor_11_out, A12, B12);
  xor xor_12 (xor_12_out, A1, B1);
  and and_12 (and_12_out, A1, B1);
  xor xor_13 (xor_13_out, A3, B3);
  or or_4 (or_4_out, and_8_out, and_7_out);
  xor xor_14 (S8, xor_8_out, or_12_out);
  xor xor_15 (S10, xor_10_out, or_13_out);
  and and_13 (and_13_out, xor_10_out, or_13_out);
  and and_14 (and_14_out, xor_11_out, A12);
  and and_15 (and_15_out, A12, B12);
  xor xor_16 (S1, xor_12_out, or_1_out);
  and and_16 (and_16_out, xor_12_out, or_1_out);
  and and_17 (and_17_out, xor_13_out, or_2_out);
  and and_18 (and_18_out, A3, B3);
  xor xor_17 (xor_17_out, A5, B5);
  or or_5 (or_5_out, and_9_out, and_10_out);
  or or_6 (or_6_out, and_13_out, and_11_out);
  xor xor_18 (S12, xor_11_out, A12);
  xor xor_19 (xor_19_out, A14, B14);
  and and_19 (and_19_out, A14, B14);
  or or_7 (or_7_out, and_16_out, and_12_out);
  xor xor_20 (S3, xor_13_out, or_2_out);
  and and_20 (and_20_out, xor_17_out, or_3_out);
  and and_21 (and_21_out, A5, B5);
  xor xor_21 (xor_21_out, A7, B7);
  or or_8 (or_8_out, and_14_out, and_15_out);
  xor xor_22 (S14, xor_19_out, A14);
  and and_22 (and_22_out, xor_19_out, A14);
  or or_9 (A4, and_17_out, and_18_out);
  xor xor_23 (S5, xor_17_out, or_3_out);
  or or_10 (A6, and_20_out, and_21_out);
  and and_23 (and_23_out, xor_21_out, or_4_out);
  and and_24 (and_24_out, A7, B7);
  xor xor_24 (xor_24_out, A9, B9);
  and and_25 (and_25_out, A9, B9);
  xor xor_25 (xor_25_out, A11, B11);
  or or_11 (or_11_out, and_22_out, and_19_out);
  xor xor_26 (S7, xor_21_out, or_4_out);
  or or_12 (or_12_out, and_23_out, and_24_out);
  xor xor_27 (S9, xor_24_out, or_5_out);
  and and_26 (and_26_out, xor_24_out, or_5_out);
  and and_27 (and_27_out, xor_25_out, or_6_out);
  and and_28 (and_28_out, A11, B11);
  xor xor_28 (xor_28_out, A13, B13);
  or or_13 (or_13_out, and_26_out, and_25_out);
  xor xor_29 (S11, xor_25_out, or_6_out);
  and and_29 (and_29_out, xor_28_out, or_8_out);
  and and_30 (and_30_out, A13, B13);
  xor xor_30 (xor_30_out, A15, B15);
  or or_14 (A12, and_27_out, and_28_out);
  xor xor_31 (S13, xor_28_out, or_8_out);
  or or_15 (A14, and_29_out, and_30_out);
  and and_31 (and_31_out, xor_30_out, or_11_out);
  and and_32 (and_32_out, A15, B15);
  xor xor_32 (S15, xor_30_out, or_11_out);
  or or_16 (or_16_out, and_31_out, and_32_out);
  xor xor_33 (xor_33_out, A16, B16);
  and and_33 (and_33_out, A16, B16);
  xor xor_34 (xor_34_out, A18, B18);
  xor xor_35 (S16, xor_33_out, or_16_out);
  and and_34 (and_34_out, xor_33_out, or_16_out);
  and and_35 (and_35_out, xor_34_out, or_23_out);
  and and_36 (and_36_out, A18, B18);
  xor xor_36 (xor_36_out, A20, B20);
  or or_17 (or_17_out, and_34_out, and_33_out);
  xor xor_37 (S18, xor_34_out, or_23_out);
  and and_37 (and_37_out, xor_36_out, A20);
  and and_38 (and_38_out, A20, B20);
  xor xor_38 (xor_38_out, A22, B22);
  or or_18 (or_18_out, and_35_out, and_36_out);
  xor xor_39 (S20, xor_36_out, A20);
  and and_39 (and_39_out, xor_38_out, A22);
  and and_40 (and_40_out, A22, B22);
  xor xor_40 (xor_40_out, A24, B24);
  and and_41 (and_41_out, A24, B24);
  xor xor_41 (xor_41_out, A26, B26);
  xor xor_42 (xor_42_out, A17, B17);
  or or_19 (or_19_out, and_37_out, and_38_out);
  xor xor_43 (S22, xor_38_out, A22);
  xor xor_44 (S24, xor_40_out, or_28_out);
  and and_42 (and_42_out, xor_40_out, or_28_out);
  and and_43 (and_43_out, xor_41_out, or_29_out);
  and and_44 (and_44_out, A26, B26);
  xor xor_45 (xor_45_out, A28, B28);
  and and_45 (and_45_out, xor_42_out, or_17_out);
  and and_46 (and_46_out, A17, B17);
  xor xor_46 (xor_46_out, A19, B19);
  or or_20 (or_20_out, and_39_out, and_40_out);
  or or_21 (or_21_out, and_42_out, and_41_out);
  xor xor_47 (S26, xor_41_out, or_29_out);
  and and_47 (and_47_out, xor_45_out, A28);
  and and_48 (and_48_out, A28, B28);
  xor xor_48 (xor_48_out, A30, B30);
  xor xor_49 (S17, xor_42_out, or_17_out);
  and and_49 (and_49_out, xor_46_out, or_18_out);
  and and_50 (and_50_out, A19, B19);
  xor xor_50 (xor_50_out, A21, B21);
  and and_51 (and_51_out, A21, B21);
  or or_22 (or_22_out, and_43_out, and_44_out);
  xor xor_51 (S28, xor_45_out, A28);
  and and_52 (and_52_out, xor_48_out, A30);
  and and_53 (and_53_out, A30, B30);
  or or_23 (or_23_out, and_45_out, and_46_out);
  xor xor_52 (S19, xor_46_out, or_18_out);
  or or_24 (A20, and_49_out, and_50_out);
  xor xor_53 (S21, xor_50_out, or_19_out);
  and and_54 (and_54_out, xor_50_out, or_19_out);
  xor xor_54 (xor_54_out, A23, B23);
  and and_55 (and_55_out, A23, B23);
  xor xor_55 (xor_55_out, A25, B25);
  or or_25 (or_25_out, and_47_out, and_48_out);
  xor xor_56 (S30, xor_48_out, A30);
  or or_26 (A22, and_54_out, and_51_out);
  xor xor_57 (S23, xor_54_out, or_20_out);
  and and_56 (and_56_out, xor_54_out, or_20_out);
  and and_57 (and_57_out, xor_55_out, or_21_out);
  and and_58 (and_58_out, A25, B25);
  xor xor_58 (xor_58_out, A27, B27);
  or or_27 (or_27_out, and_52_out, and_53_out);
  or or_28 (or_28_out, and_56_out, and_55_out);
  xor xor_59 (S25, xor_55_out, or_21_out);
  and and_59 (and_59_out, xor_58_out, or_22_out);
  and and_60 (and_60_out, A27, B27);
  xor xor_60 (xor_60_out, A29, B29);
  and and_61 (and_61_out, A29, B29);
  or or_29 (or_29_out, and_57_out, and_58_out);
  xor xor_61 (S27, xor_58_out, or_22_out);
  or or_30 (A28, and_59_out, and_60_out);
  xor xor_62 (S29, xor_60_out, or_25_out);
  and and_62 (and_62_out, xor_60_out, or_25_out);
  xor xor_63 (xor_63_out, A31, B31);
  and and_63 (and_63_out, A31, B31);
  or or_31 (A30, and_62_out, and_61_out);
  xor xor_64 (S31, xor_63_out, or_27_out);
  and and_64 (and_64_out, xor_63_out, or_27_out);
  or or_32 (Cout, and_64_out, and_63_out);

  // Notes on the sheet:
  //   AYUSH MISHRA
  //   ROLL NO.: 2106047
endmodule
