// Logisim project 2106047_AYUSH_LAB4(2).circ as structural Verilog: 1 circuit, main circuit main
module main (
  input  CTRL,
  input  [31:0] in_2,
  input  [31:0] in_3,
  output [31:0] out_4,
  output [31:0] out_5
);

  wire [31:0] divider_1_out, multiplier_1_out, multiplier_2_out;

  // Probe on in_2
  // Probe on in_3
  Multiplier #(.width(32)) multiplier_1 (.a(in_2), .b(in_3), .out(multiplier_1_out));  // open: cin, cout
  Divider #(.width(32)) divider_1 (.a(in_2), .b(in_3), .out(divider_1_out));  // open: upper, rem
  Multiplexer #(.width(32)) multiplexer_1 (
    .in0(multiplier_1_out), .in1(divider_1_out), .out(out_4), .sel(CTRL));  // open: en
  Multiplier #(.width(32)) multiplier_2 (.a(divider_1_out), .b(in_3), .out(multiplier_2_out));  // open: cin, cout
  Subtractor #(.width(32)) subtractor_1 (.a(in_2), .b(multiplier_2_out), .out(out_5));  // open: bin, bout
  // Probe on out_4
  // Probe on out_5

  // Notes on the sheet:
  //   INPUT 1
  //   MULTIPLIER & DIVIDEND
  //   INPUT 2
  //   MULTIPLICAND & DIVISOR
  //   AYUSH MISHRA -2106047 -LAB4
  //   32-bit MULTIPLIER AND DIVIDER CIRCUIT
  //   AYUSH MISHRA -2106047 -LAB4
  //   0= MULTIPLY
  //   & 1=  DIVIDE
  //   PRODUCT & QUOTIENT
  //   REMAINDER
  //   ONLY CONSIDER FOR DIVISION OR WHEN CTRL=1
  //   OUTPUT
endmodule
