// Logisim project 2106047_AYUSH_LAB5_FPU ADDER.circ as structural Verilog: 1 circuit, main circuit main
module main (
  input  [31:0] in_1,
  input  [31:0] in_2,
  output [31:0] out_3,
  output Overflow
);

  wire adder_3_cout, comparator_1_gt, comparator_2_eq, comparator_3_gt, multiplexer_3_out;
  wire [7:0] adder_1_out, adder_2_out, multiplexer_1_out, multiplexer_2_out, subtractor_1_out,
       subtractor_2_out, subtractor_3_out;

  // Probe on in_1
  // Probe on in_2
  xor xor_1 (out_3[31], in_2[31], in_1[31]);
  Comparator comparator_1 (.a(in_1[30:23]), .b(in_2[30:23]), .gt(comparator_1_gt));  // open: eq, lt
  Adder adder_1 (.a(in_1[30:23]), .b(8'h1), .out(adder_1_out));  // open: cin, cout
  Adder adder_2 (.a(in_2[30:23]), .b(8'h1), .out(adder_2_out));  // open: cin, cout
  Adder #(.width(23)) adder_3 (.a(in_1[22:0]), .b(in_2[22:0]), .out(out_3[22:0]), .cout(adder_3_cout));  // open: cin
  Multiplexer #(.width(8), .enable("false")) multiplexer_1 (
    .in0(adder_1_out), .in1(adder_2_out), .out(multiplexer_1_out), .sel(comparator_1_gt));
  Multiplexer #(.width(8), .enable("false")) multiplexer_2 (
    .in0(in_1[30:23]), .in1(in_2[30:23]), .out(multiplexer_2_out), .sel(comparator_1_gt));
  Comparator #(.width(1)) comparator_2 (.a(adder_3_cout), .b(1'b0), .eq(comparator_2_eq));  // open: gt, lt
  Subtractor subtractor_1 (.a(in_2[30:23]), .b(in_1[30:23]), .out(subtractor_1_out));  // open: bin, bout
  Comparator comparator_3 (.a(multiplexer_1_out), .b({8{1'b1}}), .gt(comparator_3_gt));  // open: eq, lt
  Subtractor subtractor_2 (.a({8{1'b0}}), .b(subtractor_1_out), .out(subtractor_2_out));  // open: bin, bout
  Multiplexer #(.enable("false")) multiplexer_3 (
    .in0(1'b1), .in1(1'b0), .out(multiplexer_3_out), .sel(comparator_3_gt));
  Subtractor subtractor_3 (.a(multiplexer_2_out), .b(subtractor_2_out), .out(subtractor_3_out));  // open: bin, bout
  Multiplexer #(.width(8), .enable("false")) multiplexer_4 (
    .in0(multiplexer_1_out), .in1(subtractor_3_out), .out(out_3[30:23]), .sel(comparator_2_eq));
  and and_1 (Overflow, multiplexer_3_out, out_3[31]);
  // Probe on out_3

  // Notes on the sheet:
  //   INPUT 1
  //   INPUT 2
  //   32-BIT FLOATING POINT UNIT ADDER
  //   AYUSH MISHRA -2106047 -LAB4
  //   4-LSB ARE CONSIDER 
  //   IT FOR SINGLE PRECISION 
  //   (i.e, 0000-1010) ONLY
  //   OUTPUT 
endmodule
