// Logisim project 2106047_AYUSH_Lab2(1).circ as structural Verilog: 1 circuit, main circuit main
module main (
  input  in_1,
  input  in_2,
  input  B16,
  input  B0,
  input  B8,
  input  B24,
  input  A16,
  input  A0,
  input  A8,
  input  A24,
  input  B17,
  input  B1,
  input  B9,
  input  B25,
  input  A17,
  input  A1,
  input  A9,
  input  B18,
  input  A25,
  input  B2,
  input  B10,
  input  B26,
  input  A18,
  input  A2,
  input  A10,
  input  B19,
  input  A26,
  input  B3,
  input  B11,
  input  B27,
  input  A19,
  input  A3,
  input  A11,
  input  A27,
  input  B20,
  input  B4,
  input  B12,
  input  B28,
  input  A20,
  input  A4,
  input  A12,
  input  A28,
  input  B21,
  input  B5,
  input  B13,
  input  B29,
  input  A21,
  input  A5,
  input  A13,
  input  B22,
  input  A29,
  input  B6,
  input  B14,
  input  B30,
  input  A22,
  input  A6,
  input  A14,
  input  B23,
  input  A30,
  input  B7,
  input  B15,
  input  B31,
  input  A23,
  input  A7,
  input  A15,
  input  A31,
  output D16,
  output D0,
  output D8,
  output D24,
  output D17,
  output D1,
  output D9,
  output D25,
  output D18,
  output D2,
  output D10,
  output D26,
  output D19,
  output D3,
  output D11,
  output D27,
  output D20,
  output D4,
  output D12,
  output D28,
  output D21,
  output D5,
  output D13,
  output D29,
  output D22,
  output D6,
  output D14,
  output D30,
  output D23,
  output D7,
  output D15,
  output D31,
  output carry_out,
  output overflow
);

  wire adder_1_cout, adder_2_cout, adder_3_cout, adder_4_cout, adder_5_cout, adder_6_cout, adder_7_cout,
       adder_8_cout, adder_9_cout, adder_10_cout, adder_11_cout, adder_12_cout, adder_13_cout, adder_14_cout,
       adder_15_cout, adder_16_cout, adder_17_cout, adder_18_cout, adder_19_cout, adder_20_cout,
       adder_21_cout, adder_22_cout, adder_23_cout, adder_24_cout, adder_25_cout, adder_26_cout,
       adder_27_cout, adder_28_cout, adder_29_cout, adder_30_cout, adder_31_cout, adder_32_cout, xor_1_out,
       xor_2_out, xor_3_out, xor_4_out, xor_5_out, xor_6_out, xor_7_out, xor_8_out, xor_9_out, xor_10_out,
       xor_11_out, xor_12_out, xor_13_out, xor_14_out, xor_15_out, xor_16_out, xor_17_out, xor_18_out,
       xor_19_out, xor_20_out, xor_21_out, xor_22_out, xor_23_out, xor_24_out, xor_25_out, xor_26_out,
       xor_27_out, xor_28_out, xor_29_out, xor_30_out, xor_31_out, xor_32_out, xor_33_out;

  xor xor_1 (xor_1_out, in_1, in_2);
  xor xor_2 (xor_2_out, B0, in_1);
  xor xor_3 (xor_3_out, B1, in_1);
  xor xor_4 (xor_4_out, B2, in_1);
  xor xor_5 (xor_5_out, B3, in_1);
  xor xor_6 (xor_6_out, B4, in_1);
  xor xor_7 (xor_7_out, B5, in_1);
  xor xor_8 (xor_8_out, B6, in_1);
  xor xor_9 (xor_9_out, B7, in_1);
  Adder #(.width(1)) adder_1 (.a(xor_2_out), .b(A0), .out(D0), .cin(xor_1_out), .cout(adder_1_cout));
  Adder #(.width(1)) adder_2 (.a(xor_3_out), .b(A1), .out(D1), .cin(adder_1_cout), .cout(adder_2_cout));
  Adder #(.width(1)) adder_3 (.a(xor_4_out), .b(A2), .out(D2), .cin(adder_2_cout), .cout(adder_3_cout));
  Adder #(.width(1)) adder_4 (.a(xor_5_out), .b(A3), .out(D3), .cin(adder_3_cout), .cout(adder_4_cout));
  Adder #(.width(1)) adder_5 (.a(xor_6_out), .b(A4), .out(D4), .cin(adder_4_cout), .cout(adder_5_cout));
  Adder #(.width(1)) adder_6 (.a(xor_7_out), .b(A5), .out(D5), .cin(adder_5_cout), .cout(adder_6_cout));
  Adder #(.width(1)) adder_7 (.a(xor_8_out), .b(A6), .out(D6), .cin(adder_6_cout), .cout(adder_7_cout));
  Adder #(.width(1)) adder_8 (.a(xor_9_out), .b(A7), .out(D7), .cin(adder_7_cout), .cout(adder_8_cout));
  xor xor_10 (xor_10_out, B8, in_1);
  xor xor_11 (xor_11_out, B9, in_1);
  xor xor_12 (xor_12_out, B10, in_1);
  xor xor_13 (xor_13_out, B11, in_1);
  xor xor_14 (xor_14_out, B12, in_1);
  xor xor_15 (xor_15_out, B13, in_1);
  xor xor_16 (xor_16_out, B14, in_1);
  xor xor_17 (xor_17_out, B15, in_1);
  Adder #(.width(1)) adder_9 (.a(xor_10_out), .b(A8), .out(D8), .cin(adder_8_cout), .cout(adder_9_cout));
  Adder #(.width(1)) adder_10 (.a(xor_11_out), .b(A9), .out(D9), .cin(adder_9_cout), .cout(adder_10_cout));
  Adder #(.width(1)) adder_11 (.a(xor_12_out), .b(A10), .out(D10), .cin(adder_10_cout), .cout(adder_11_cout));
  Adder #(.width(1)) adder_12 (.a(xor_13_out), .b(A11), .out(D11), .cin(adder_11_cout), .cout(adder_12_cout));
  Adder #(.width(1)) adder_13 (.a(xor_14_out), .b(A12), .out(D12), .cin(adder_12_cout), .cout(adder_13_cout));
  Adder #(.width(1)) adder_14 (.a(xor_15_out), .b(A13), .out(D13), .cin(adder_13_cout), .cout(adder_14_cout));
  Adder #(.width(1)) adder_15 (.a(xor_16_out), .b(A14), .out(D14), .cin(adder_14_cout), .cout(adder_15_cout));
  Adder #(.width(1)) adder_16 (.a(xor_17_out), .b(A15), .out(D15), .cin(adder_15_cout), .cout(adder_16_cout));
  xor xor_18 (xor_18_out, B16, in_1);
  xor xor_19 (xor_19_out, B17, in_1);
  xor xor_20 (xor_20_out, B18, in_1);
  xor xor_21 (xor_21_out, B19, in_1);
  xor xor_22 (xor_22_out, B20, in_1);
  xor xor_23 (xor_23_out, B21, in_1);
  xor xor_24 (xor_24_out, B22, in_1);
  xor xor_25 (xor_25_out, B23, in_1);
  Adder #(.width(1)) adder_17 (.a(xor_18_out), .b(A16), .out(D16), .cin(adder_16_cout), .cout(adder_17_cout));
  Adder #(.width(1)) adder_18 (.a(xor_19_out), .b(A17), .out(D17), .cin(adder_17_cout), .cout(adder_18_cout));
  Adder #(.width(1)) adder_19 (.a(xor_20_out), .b(A18), .out(D18), .cin(adder_18_cout), .cout(adder_19_cout));
  Adder #(.width(1)) adder_20 (.a(xor_21_out), .b(A19), .out(D19), .cin(adder_19_cout), .cout(adder_20_cout));
  Adder #(.width(1)) adder_21 (.a(xor_22_out), .b(A20), .out(D20), .cin(adder_20_cout), .cout(adder_21_cout));
  Adder #(.width(1)) adder_22 (.a(xor_23_out), .b(A21), .out(D21), .cin(adder_21_cout), .cout(adder_22_cout));
  Adder #(.width(1)) adder_23 (.a(xor_24_out), .b(A22), .out(D22), .cin(adder_22_cout), .cout(adder_23_cout));
  Adder #(.width(1)) adder_24 (.a(xor_25_out), .b(A23), .out(D23), .cin(adder_23_cout), .cout(adder_24_cout));
  xor xor_26 (xor_26_out, B24, in_1);
  xor xor_27 (xor_27_out, B25, in_1);
  xor xor_28 (xor_28_out, B26, in_1);
  xor xor_29 (xor_29_out, B27, in_1);
  xor xor_30 (xor_30_out, B28, in_1);
  xor xor_31 (xor_31_out, B29, in_1);
  xor xor_32 (xor_32_out, B30, in_1);
  xor xor_33 (xor_33_out, B31, in_1);
  Adder #(.width(1)) adder_25 (.a(xor_26_out), .b(A24), .out(D24), .cin(adder_24_cout), .cout(adder_25_cout));
  Adder #(.width(1)) adder_26 (.a(xor_27_out), .b(A25), .out(D25), .cin(adder_25_cout), .cout(adder_26_cout));
  Adder #(.width(1)) adder_27 (.a(xor_28_out), .b(A26), .out(D26), .cin(adder_26_cout), .cout(adder_27_cout));
  Adder #(.width(1)) adder_28 (.a(xor_29_out), .b(A27), .out(D27), .cin(adder_27_cout), .cout(adder_28_cout));
  Adder #(.width(1)) adder_29 (.a(xor_30_out), .b(A28), .out(D28), .cin(adder_28_cout), .cout(adder_29_cout));
  Adder #(.width(1)) adder_30 (.a(xor_31_out), .b(A29), .out(D29), .cin(adder_29_cout), .cout(adder_30_cout));
  Adder #(.width(1)) adder_31 (.a(xor_32_out), .b(A30), .out(D30), .cin(adder_30_cout), .cout(adder_31_cout));
  Adder #(.width(1)) adder_32 (.a(xor_33_out), .b(A31), .out(D31), .cin(adder_31_cout), .cout(adder_32_cout));
  xor xor_34 (carry_out, adder_32_cout, in_1);
  xor xor_35 (overflow, adder_31_cout, adder_32_cout);

  // Notes on the sheet:
  //   carry in
  //   32-bit ADDER-SUBSTRACTOR USING FULL ADDER
  //   -600491 & 287632
  //   2106047: AYUSH MISHRA
endmodule
