// Logisim project 4 BIT DIVISION CIRCUIT.circ as structural Verilog: 1 circuit, main circuit main
module main (
  input  M0,
  input  M1,
  input  M2,
  input  M3,
  input  Q3,
  input  Q2,
  input  Q1,
  input  Q0,
  input  Dv7,
  input  Dv6,
  input  Dv5,
  input  Dv4,
  input  DR0,
  input  DR1,
  input  DR2,
  input  DR3,
  input  MUL_DIV,
  input  ENABLE,
  input  Clk1_Clk2,
  output Asign,
  output A3,
  output A2,
  output A1,
  output A0,
  output Q3_2,
  output Q2_2,
  output Q1_2,
  output Q0_2
);

  wire adder_1_cout, adder_1_out, adder_2_cout, adder_2_out, adder_3_cout, adder_3_out, adder_4_out,
       and_1_out, and_2_out, and_3_out, and_4_out, and_5_out, and_6_out, and_8_out, and_9_out, and_10_out,
       and_11_out, and_12_out, and_13_out, and_14_out, and_15_out, CLOCK_out, d_ff_1_qn, d_ff_2_q, d_ff_3_q,
       d_ff_4_q, d_ff_5_q, d_ff_6_q, d_ff_7_q, d_ff_8_q, d_ff_9_q, d_ff_10_q, multiplexer_1_out,
       multiplexer_2_out, multiplexer_4_out, multiplexer_5_out, multiplexer_7_out, multiplexer_13_out,
       not_1_out, not_2_out, or_1_out, or_2_out, or_3_out, or_4_out, or_5_out, or_6_out, or_7_out, or_8_out,
       or_9_out, undriven, undriven_2, xnor_1_out, xor_1_out, xor_2_out, xor_3_out, xor_4_out, xor_5_out,
       xor_6_out, xor_7_out, xor_8_out, xor_9_out;

  xor xor_1 (xor_1_out, DR0, xnor_1_out);
  xor xor_2 (xor_2_out, DR1, xnor_1_out);
  xor xor_3 (xor_3_out, DR2, xnor_1_out);
  xor xor_4 (xor_4_out, DR3, xnor_1_out);
  xnor xnor_1 (xnor_1_out, DR3, Asign);
  and and_1 (and_1_out, xor_5_out, M0);
  and and_2 (and_2_out, xor_5_out, M1);
  and and_3 (and_3_out, xor_5_out, M2);
  and and_4 (and_4_out, xor_5_out, M3);
  xor xor_5 (xor_5_out, d_ff_10_q, Q0_2);
  and and_5 (and_5_out, xor_5_out, Q0_2);
  Clock CLOCK (.out(CLOCK_out));
  D_Flip_Flop #(.trigger("falling")) d_ff_1 (.clk(CLOCK_out), .D(1'b1), .Qn(d_ff_1_qn));  // open: Q, preset, en, reset
  and and_6 (and_6_out, d_ff_1_qn, Dv7);
  or or_1 (or_1_out, adder_4_out, and_6_out);
  xor xor_6 (xor_6_out, and_5_out, and_1_out);
  xor xor_7 (xor_7_out, and_5_out, and_2_out);
  xor xor_8 (xor_8_out, and_5_out, and_3_out);
  xor xor_9 (xor_9_out, and_5_out, and_4_out);
  D_Flip_Flop d_ff_2 (.clk(CLOCK_out), .D(or_1_out), .Q(d_ff_2_q));  // open: Qn, preset, en, reset
  and and_7 (Asign, d_ff_2_q, MUL_DIV);
  Multiplexer multiplexer_1 (.in0(xor_6_out), .in1(xor_1_out), .out(multiplexer_1_out), .sel(MUL_DIV), .en(ENABLE));
  Multiplexer multiplexer_2 (.in0(xor_7_out), .in1(xor_2_out), .out(multiplexer_2_out), .sel(MUL_DIV), .en(ENABLE));
  and and_8 (and_8_out, d_ff_1_qn, Dv6);
  or or_2 (or_2_out, adder_3_out, and_8_out);
  Multiplexer multiplexer_3 (.in0(d_ff_2_q), .in1(d_ff_3_q), .out(A3), .sel(MUL_DIV), .en(ENABLE));
  Multiplexer multiplexer_4 (.in0(xor_8_out), .in1(xor_3_out), .out(multiplexer_4_out), .sel(MUL_DIV), .en(ENABLE));
  Multiplexer multiplexer_5 (.in0(xor_9_out), .in1(xor_4_out), .out(multiplexer_5_out), .sel(MUL_DIV), .en(ENABLE));
  and and_9 (and_9_out, d_ff_1_qn, Dv5);
  D_Flip_Flop d_ff_3 (.clk(CLOCK_out), .D(or_2_out), .Q(d_ff_3_q));  // open: Qn, preset, en, reset
  or or_3 (or_3_out, adder_2_out, and_9_out);
  Multiplexer multiplexer_6 (.in0(d_ff_2_q), .in1(d_ff_4_q), .out(A2), .sel(MUL_DIV), .en(ENABLE));
  Multiplexer multiplexer_7 (.in0(and_5_out), .in1(xnor_1_out), .out(multiplexer_7_out), .sel(MUL_DIV), .en(ENABLE));
  Adder #(.width(1)) adder_1 (
    .a(multiplexer_1_out), .b(A0), .out(adder_1_out), .cin(multiplexer_7_out), .cout(adder_1_cout));
  Adder #(.width(1)) adder_2 (
    .a(multiplexer_2_out), .b(A1), .out(adder_2_out), .cin(adder_1_cout), .cout(adder_2_cout));
  Adder #(.width(1)) adder_3 (
    .a(multiplexer_4_out), .b(A2), .out(adder_3_out), .cin(adder_2_cout), .cout(adder_3_cout));
  Adder #(.width(1)) adder_4 (.a(multiplexer_5_out), .b(A3), .out(adder_4_out), .cin(adder_3_cout));  // open: cout
  and and_10 (and_10_out, d_ff_1_qn, Dv4);
  D_Flip_Flop d_ff_4 (.clk(CLOCK_out), .D(or_3_out), .Q(d_ff_4_q));  // open: Qn, preset, en, reset
  or or_4 (or_4_out, adder_1_out, and_10_out);
  D_Flip_Flop d_ff_5 (.clk(CLOCK_out), .D(or_4_out), .Q(d_ff_5_q));  // open: Qn, preset, en, reset
  Multiplexer multiplexer_8 (.in0(d_ff_3_q), .in1(d_ff_5_q), .out(A1), .sel(MUL_DIV), .en(ENABLE));
  and and_11 (and_11_out, d_ff_1_qn, Q3);
  or or_5 (or_5_out, Q3_2, and_11_out);
  Multiplexer multiplexer_9 (.in0(d_ff_4_q), .in1(d_ff_6_q), .out(A0), .sel(MUL_DIV), .en(ENABLE));
  and and_12 (and_12_out, d_ff_1_qn, Q2);
  D_Flip_Flop #(.trigger("falling")) d_ff_6 (
    .clk(CLOCK_out), .D(or_5_out), .Q(d_ff_6_q));  // open: Qn, preset, en, reset
  or or_6 (or_6_out, Q2_2, and_12_out);
  D_Flip_Flop #(.trigger("falling")) d_ff_7 (
    .clk(CLOCK_out), .D(or_6_out), .Q(d_ff_7_q), .preset(undriven));  // open: Qn, en, reset
  Multiplexer multiplexer_10 (.in0(d_ff_5_q), .in1(d_ff_7_q), .out(Q3_2), .sel(MUL_DIV), .en(ENABLE));
  and and_13 (and_13_out, d_ff_1_qn, Q1);
  D_Flip_Flop #(.trigger("falling")) d_ff_8 (
    .clk(CLOCK_out), .D(or_7_out), .Q(d_ff_8_q));  // open: Qn, preset, en, reset
  or or_7 (or_7_out, Q1_2, and_13_out);
  Multiplexer multiplexer_11 (.in0(d_ff_6_q), .in1(d_ff_8_q), .out(Q2_2), .sel(MUL_DIV), .en(ENABLE));
  and and_14 (and_14_out, d_ff_1_qn, Q0);
  or or_8 (or_8_out, Q0_2, and_14_out);
  Multiplexer multiplexer_12 (.in0(d_ff_7_q), .in1(multiplexer_13_out), .out(Q1_2), .sel(MUL_DIV), .en(ENABLE));
  not not_1 (not_1_out, A3);
  D_Flip_Flop #(.trigger("falling")) d_ff_9 (
    .clk(CLOCK_out), .D(or_8_out), .Q(d_ff_9_q));  // open: Qn, preset, en, reset
  Multiplexer multiplexer_13 (
    .in0(d_ff_9_q), .in1(not_1_out), .out(multiplexer_13_out), .sel(Clk1_Clk2), .en(undriven_2));
  or or_9 (or_9_out, d_ff_9_q, and_15_out);
  Multiplexer multiplexer_14 (.in0(d_ff_8_q), .in1(1'b0), .out(Q0_2), .sel(MUL_DIV), .en(ENABLE));
  and and_15 (and_15_out, d_ff_1_qn, 1'b0);
  not not_2 (not_2_out, MUL_DIV);
  D_Flip_Flop #(.trigger("falling")) d_ff_10 (
    .clk(CLOCK_out), .D(or_9_out), .Q(d_ff_10_q), .en(not_2_out));  // open: Qn, preset, reset

  // Notes on the sheet:
  //   MULTIPLICAND
  //   DIVISOR
  //   REMAINDER
  //   (Dv3)
  //   AYUSH MISHRA, ROLL NUMBER:2106047
  //   (Dv2)
  //   4-BIT MULTIPLIER/DIVISION CIRCUIT
  //   DIVIDEND
  //   (Dv1)
  //   / MULTIPLIER
  //   (Dv0)
  //   QUOTIENT
endmodule
